// Logisim project adders.circ as structural Verilog: 3 circuits, main circuit main
module main (
  input  [7:0] x1,
  input  [7:0] x2,
  output [7:0] s,
  output co
);

  wire full_adder_1_co, full_adder_2_co, full_adder_3_co, full_adder_4_co, full_adder_5_co, full_adder_6_co,
       full_adder_7_co;

  full_adder full_adder_1 (.x1(x1[0]), .x2(x2[0]), .co(full_adder_1_co), .s(s[0]));  // open: ci
  full_adder full_adder_2 (.x1(x1[1]), .x2(x2[1]), .ci(full_adder_1_co), .co(full_adder_2_co), .s(s[1]));
  full_adder full_adder_3 (.x1(x1[2]), .x2(x2[2]), .ci(full_adder_2_co), .co(full_adder_3_co), .s(s[2]));
  full_adder full_adder_4 (.x1(x1[3]), .x2(x2[3]), .ci(full_adder_3_co), .co(full_adder_4_co), .s(s[3]));
  full_adder full_adder_5 (.x1(x1[4]), .x2(x2[4]), .ci(full_adder_4_co), .co(full_adder_5_co), .s(s[4]));
  full_adder full_adder_6 (.x1(x1[5]), .x2(x2[5]), .ci(full_adder_5_co), .co(full_adder_6_co), .s(s[5]));
  full_adder full_adder_7 (.x1(x1[6]), .x2(x2[6]), .ci(full_adder_6_co), .co(full_adder_7_co), .s(s[6]));
  full_adder full_adder_8 (.x1(x1[7]), .x2(x2[7]), .ci(full_adder_7_co), .co(co), .s(s[7]));

  // Notes on the sheet:
  //   Assignment: Logisim Adders
endmodule

module half_adder (
  input  x1,
  input  x2,
  output s,
  output co
);

  and and_1 (co, x2, x1);
  xor xor_1 (s, x1, x2);
endmodule

module full_adder (
  input  ci,
  input  x1,
  input  x2,
  output s,
  output co
);

  wire and_1_out, and_2_out, xor_1_out;

  xor xor_1 (xor_1_out, x1, x2);
  and and_1 (and_1_out, x1, x2);
  and and_2 (and_2_out, ci, xor_1_out);
  or or_1 (co, and_1_out, and_2_out);
  xor xor_2 (s, xor_1_out, ci);
endmodule
