// Logisim project complete-4-bit-alu.circ as structural Verilog: 4 circuits, main circuit 4-bit ALU
// 1b ALU
module _1_bit_ALU (
  input  a_invert,
  input  b_invert,
  input  c_in,
  input  [1:0] operation,
  input  a,
  input  less,
  input  b,
  output result,
  output c_out
);

  wire adder_1_out, and_1_out, multiplexer_1_out, multiplexer_2_out, not_1_out, not_2_out, or_1_out;

  Multiplexer #(.enable("false")) multiplexer_1 (.in0(a), .in1(not_1_out), .out(multiplexer_1_out), .sel(a_invert));
  not not_1 (not_1_out, a);
  Multiplexer #(.enable("false")) multiplexer_2 (.in0(b), .in1(not_2_out), .out(multiplexer_2_out), .sel(b_invert));
  not not_2 (not_2_out, b);
  and and_1 (and_1_out, multiplexer_1_out, multiplexer_2_out);
  or or_1 (or_1_out, multiplexer_1_out, multiplexer_2_out);
  Adder #(.width(1)) adder_1 (
    .a(multiplexer_1_out), .b(multiplexer_2_out), .out(adder_1_out), .cin(c_in), .cout(c_out));
  Multiplexer #(.select(2), .enable("false")) multiplexer_3 (
    .in0(and_1_out), .in1(or_1_out), .in2(adder_1_out), .in3(less), .out(result), .sel(operation));
endmodule

// 4b ALU
module _4_bit_ALU (
  input  b_invert,
  input  c_in,
  input  a_invert,
  input  [1:0] operation,
  input  [3:0] a,
  input  [3:0] b,
  output [3:0] result,
  output overflow,
  output c_out
);

  wire msb_alu_1_set, n1_bit_alu_1_c_out, n1_bit_alu_2_c_out, n1_bit_alu_3_c_out;

  _1_bit_ALU u_1_bit_alu_1 (
    .a(a[0]), .result(result[0]), .b_invert(b_invert), .c_in(c_in), .operation(operation),
    .c_out(n1_bit_alu_1_c_out), .b(b[0]), .a_invert(a_invert), .less(msb_alu_1_set));
  _1_bit_ALU u_1_bit_alu_2 (
    .a(a[1]), .result(result[1]), .b_invert(b_invert), .c_in(n1_bit_alu_1_c_out), .operation(operation),
    .c_out(n1_bit_alu_2_c_out), .b(b[1]), .a_invert(a_invert), .less(1'b0));
  _1_bit_ALU u_1_bit_alu_3 (
    .a(a[2]), .result(result[2]), .b_invert(b_invert), .c_in(n1_bit_alu_2_c_out), .operation(operation),
    .c_out(n1_bit_alu_3_c_out), .b(b[2]), .a_invert(a_invert), .less(1'b0));
  MSB_ALU msb_alu_1 (
    .a(a[3]), .less(1'b0), .b(b[3]), .a_invert(a_invert), .b_invert(b_invert), .c_in(n1_bit_alu_3_c_out),
    .operation(operation), .c_out(c_out), .result(result[3]), .set(msb_alu_1_set));
  overflow_detector overflow_detector_1 (.c_in(n1_bit_alu_3_c_out), .c_out(c_out), .overflow(overflow));
endmodule

module MSB_ALU (
  input  a_invert,
  input  b_invert,
  input  c_in,
  input  [1:0] operation,
  input  a,
  input  less,
  input  b,
  output result,
  output set,
  output c_out
);

  wire adder_1_out, and_1_out, multiplexer_1_out, multiplexer_2_out, not_1_out, not_2_out, not_3_out,
       or_1_out, overflow_detector_1_overflow;

  Multiplexer #(.enable("false")) multiplexer_1 (.in0(a), .in1(not_1_out), .out(multiplexer_1_out), .sel(a_invert));
  not not_1 (not_1_out, a);
  Multiplexer #(.enable("false")) multiplexer_2 (.in0(b), .in1(not_2_out), .out(multiplexer_2_out), .sel(b_invert));
  not not_2 (not_2_out, b);
  and and_1 (and_1_out, multiplexer_1_out, multiplexer_2_out);
  or or_1 (or_1_out, multiplexer_1_out, multiplexer_2_out);
  Adder #(.width(1)) adder_1 (
    .a(multiplexer_1_out), .b(multiplexer_2_out), .out(adder_1_out), .cin(c_in), .cout(c_out));
  Multiplexer #(.select(2), .enable("false")) multiplexer_3 (
    .in0(and_1_out), .in1(or_1_out), .in2(adder_1_out), .in3(less), .out(result), .sel(operation));
  overflow_detector overflow_detector_1 (.c_in(c_in), .c_out(c_out), .overflow(overflow_detector_1_overflow));
  Multiplexer #(.enable("false")) multiplexer_4 (
    .in0(adder_1_out), .in1(not_3_out), .out(set), .sel(overflow_detector_1_overflow));
  not not_3 (not_3_out, adder_1_out);
endmodule

module overflow_detector (
  input  c_in,
  input  c_out,
  output overflow
);

  xor xor_1 (overflow, c_in, c_out);
endmodule
